# Fritzing sketch Metronome Watch (saved by Fritzing 0.9.3b)

parts:
  Part4 = LilyPad Arduino USB
  Part5 = LilyPad Coin Cell Battery Holder
  R1 = Resistor [tolerance=±5% resistance=220 package=THT]
  S1 = Pushbutton [package="[THT]"]
  U1 = Vibration Motor- ROB-08449 [package=vibe-motor-10mm]
  LED1 = LEDs [package=led10mm]
  LED2 = LEDs [package=led10mm]
  Part2 = LilyPad Coin Cell Battery Holder
  R2 = Resistor [tolerance=±5% resistance=1k package="0402 [SMD]"]
  R3 = Resistor [tolerance=±5% resistance=3k package="0402 [SMD]"]

nets:
  N1: Part4.3V3, Part4.D2, S1.Pin_3, S1.Pin_4, R2.Pin_0, R3.Pin_1
  N2: Part4.GND, Part5.-, R1.Pin_1, U1.+, LED1.A, LED2.A, R3.Pin_0
  N3: Part4.A3, U1.-
  N4: Part4.D9, LED2.C
  N5: Part4.D11, LED1.C
  N6: R1.Pin_0, S1.Pin_1, S1.Pin_2
  N7: Part2.+, R2.Pin_1

notes:
  Downbeat LED
  Flashes only on the first beat
  Button used to set metronome
  4 taps are needed,
  Feedback:
  -
  Beat LED
  Flashes on all beats other than the first beat
  Vibration Motor
  Vibrates on every beat
  Feedback:
  - May include two, from Lindy's feedback
  - One on both sides of the wrist
  2 Coin Cell Batteries
  - 6V
  - lilypad needs between 3.3 - 5v, so i will use a voltage divider circuit
  Lilypad Arduino USB
  Feedback:
  - will remove the jst connector to capitalize on space
  4.5v Here
  1.5v Here
